// Logisim project Tic_Tac_Toe.circ as structural Verilog: 6 circuits, main circuit main
module main (
);

  wire P1_check, P1_state, P1a, P1b, P1c, P1d, P1e, P1f, P1g, P1h, P1i, P2_check, P2_state, P2a, P2b, P2c,
       P2d, P2e, P2f, P2g, P2h, P2i, Reset, Sia, Sib, Sic, Sid, Sie, Sif, Sig, Sih, Sii, Soa, Sob, Soc, Sod,
       Soe, Sof, Sog, Soh, Soi, tie_detect_1_out_12, Winner_p1, Winner_p2;

  // RGBLED rgbled_1: pin names not known; wires that end beside it: P1a, P2a
  Button button_1 (.out(Sia));
  // RGBLED rgbled_2: pin names not known; wires that end beside it: P1d, P2d
  Button button_2 (.out(Sid));
  // RGBLED rgbled_3: pin names not known; wires that end beside it: P1g, P2g
  Button button_3 (.out(Sig));
  // RGBLED rgbled_4: pin names not known; wires that end beside it: P1b, P2b
  // RGBLED rgbled_5: pin names not known; wires that end beside it: P1e, P2e
  // RGBLED rgbled_6: pin names not known; wires that end beside it: P1h, P2h
  Win_detect win_detect_1 (
    .I(P1i), .E(P1e), .H(P1h), .B(P1b), .F(P1f), .D(P1d), .A(P1a), .C(P1c), .G(P1g), .P1(P1_check));
  Button button_4 (.out(Sib));
  Button button_5 (.out(Sie));
  Button button_6 (.out(Sih));
  // RGBLED Winner: pin names not known; wires that end beside it: Winner_p1, Winner_p2
  Result_lock result_lock_1 (
    .P1_win(Winner_p1), .P1_check(P1_check), .P2_win(Winner_p2), .Reset(Reset), .P2_check(P2_check));
  // RGBLED rgbled_7: pin names not known; wires that end beside it: P1c, P2c
  Button button_7 (.out(Sic));
  // RGBLED rgbled_8: pin names not known; wires that end beside it: P1f, P2f
  Button button_8 (.out(Sif));
  // RGBLED rgbled_9: pin names not known; wires that end beside it: P1i, P2i
  Button button_9 (.out(Sii));
  LED Tie (.in(tie_detect_1_out_12));
  // RGBLED Player1: pin names not known; wires that end beside it: 1'b1
  // RGBLED Player2: pin names not known; wires that end beside it: 1'b1
  player_select player_select_1 (
    .Si(Soi), .Sa(Soa), .Sh(Soh), .Sb(Sob), .Sg(Sog), .Sc(Soc), .Sf(Sof), .Sd(Sod), .Se(Soe), .P2(P2_state),
    .P1(P1_state));
  Win_detect win_detect_2 (
    .I(P2i), .E(P2e), .H(P2h), .B(P2b), .F(P2f), .D(P2d), .A(P2a), .C(P2c), .G(P2g), .P1(P2_check));
  Button u_Reset (.out(Reset));
  Tie_detect tie_detect_1 (
    .Soh(Soh), .Sof(Sof), .Sod(Sod), .Sob(Sob), .Sog(Sog), .Soi(Soi), .Soa(Soa), .Soc(Soc), .Soe(Soe),
    .P1_check(P1_check), .P2_check(P2_check), .out_12(tie_detect_1_out_12));
  switch SwA (.Reset(Reset), .P1(P1a), .P2_state(P2_state), .MRclk(Sia), .P2(P2a), .SW(Soa), .P1_state(P1_state));
  switch SwD (.Reset(Reset), .P1(P1d), .P2_state(P2_state), .MRclk(Sid), .P2(P2d), .SW(Sod), .P1_state(P1_state));
  switch SwG (.Reset(Reset), .P1(P1g), .P2_state(P2_state), .MRclk(Sig), .P2(P2g), .SW(Sog), .P1_state(P1_state));
  switch SwB (.Reset(Reset), .P1(P1b), .P2_state(P2_state), .MRclk(Sib), .P2(P2b), .SW(Sob), .P1_state(P1_state));
  switch SwE (.Reset(Reset), .P1(P1e), .P2_state(P2_state), .MRclk(Sie), .P2(P2e), .SW(Soe), .P1_state(P1_state));
  switch SwH (.Reset(Reset), .P1(P1h), .P2_state(P2_state), .MRclk(Sih), .P2(P2h), .SW(Soh), .P1_state(P1_state));
  switch SwC (.Reset(Reset), .P1(P1c), .P2_state(P2_state), .MRclk(Sic), .P2(P2c), .SW(Soc), .P1_state(P1_state));
  switch SwF (.Reset(Reset), .P1(P1f), .P2_state(P2_state), .MRclk(Sif), .P2(P2f), .SW(Sof), .P1_state(P1_state));
  switch SwI (.Reset(Reset), .P1(P1i), .P2_state(P2_state), .MRclk(Sii), .P2(P2i), .SW(Soi), .P1_state(P1_state));

  // Notes on the sheet:
  //   TIC-TAC-TOE
  //   Done by:
  //   Anvay Pancholiya (1RV19EC026)
  //   Apurva D Bhargava (1RV19EC027)
endmodule

module player_select (
  input  Sa,
  input  Sb,
  input  Sc,
  input  Sd,
  input  Se,
  input  Sf,
  input  Sg,
  input  Sh,
  input  Si,
  output P2,
  output P1
);

  wire xor_1_out, xor_2_out, xor_3_out, xor_4_out, xor_5_out, xor_6_out, xor_7_out;

  xor xor_1 (xor_1_out, Sa, Sb);
  xor xor_2 (xor_2_out, Sc, Sd);
  xor xor_3 (xor_3_out, Se, Sf);
  xor xor_4 (xor_4_out, Sg, Sh);
  xor xor_5 (xor_5_out, xor_1_out, xor_2_out);
  xor xor_6 (xor_6_out, xor_3_out, xor_4_out);
  xor xor_7 (xor_7_out, xor_5_out, xor_6_out);
  xor xor_8 (P2, xor_7_out, Si);
  not not_1 (P1, P2);

  // Notes on the sheet:
  //   Player_select
endmodule

module switch (
  input  P1_state,
  input  P2_state,
  input  MRclk,
  input  Reset,
  output P1,
  output SW,
  output P2
);

  D_Flip_Flop d_ff_1 (.D(1'b1), .clk(MRclk), .Q(SW), .reset(Reset));  // open: Qn, preset
  D_Flip_Flop d_ff_2 (.D(P1_state), .clk(SW), .Q(P1), .reset(Reset));  // open: Qn, preset
  D_Flip_Flop d_ff_3 (.D(P2_state), .clk(SW), .Q(P2), .reset(Reset));  // open: Qn, preset

  // Notes on the sheet:
  //   P1: pull=down
  //   P2: pull=down
  //   Switch
endmodule

module Win_detect (
  input  A,
  input  B,
  input  C,
  input  D,
  input  E,
  input  F,
  input  G,
  input  H,
  input  I,
  output P1
);

  wire and_1_out, and_2_out, and_3_out, and_4_out, and_5_out, and_6_out, and_7_out, and_8_out;

  and and_1 (and_1_out, A, B, C);
  and and_2 (and_2_out, D, E, F);
  and and_3 (and_3_out, G, H, I);
  and and_4 (and_4_out, A, D, G);
  and and_5 (and_5_out, B, E, H);
  and and_6 (and_6_out, C, F, I);
  and and_7 (and_7_out, A, E, I);
  and and_8 (and_8_out, C, E, G);
  or or_1 (P1, and_1_out, and_2_out, and_3_out, and_4_out, and_5_out, and_6_out, and_7_out, and_8_out);

  // Notes on the sheet:
  //   Win_detect
endmodule

module Tie_detect (
  input  P1_check,
  input  P2_check,
  input  Soa,
  input  Sob,
  input  Soc,
  input  Sod,
  input  Soe,
  input  Sof,
  input  Sog,
  input  Soh,
  input  Soi,
  output out_12
);

  wire and_1_out, not_1_out;

  and and_1 (and_1_out, Soa, Sob, Soc, Sod, Soe, Sof, Sog, Soh, Soi);
  not not_1 (not_1_out, and_1_out);
  nor nor_1 (out_12, P1_check, P2_check, not_1_out);

  // Notes on the sheet:
  //   Tie_detect
endmodule

module Result_lock (
  input  P1_check,
  input  P2_check,
  input  Reset,
  output P1_win,
  output P2_win
);

  wire d_ff_1_qn, d_ff_2_qn;

  D_Flip_Flop d_ff_1 (.D(d_ff_2_qn), .clk(P1_check), .Q(P1_win), .Qn(d_ff_1_qn), .reset(Reset));  // open: preset
  D_Flip_Flop d_ff_2 (.D(d_ff_1_qn), .clk(P2_check), .Q(P2_win), .Qn(d_ff_2_qn), .reset(Reset));  // open: preset

  // Notes on the sheet:
  //   Player_select
endmodule
